// Logisim project rudimentary computing device.circ as structural Verilog: 1 circuit, main circuit main
module main (
  input  in_1,
  input  in_2,
  input  in_3,
  input  in_4,
  input  in_5,
  input  in_6,
  input  in_7,
  output [5:0] out_8
);

  wire clock_1_out;

  Clock clock_1 (.out(clock_1_out));
  LED led_1 (.in(out_8[2]));
  LED led_2 (.in(out_8[5]));
  LED led_3 (.in(out_8[4]));
  LED led_4 (.in(out_8[3]));
  program_counter_main main_1 (
    .in_7(in_1), .in_8(clock_1_out), .out_9(out_8[5]), .out_10(out_8[4]), .out_11(out_8[3]),
    .out_12(out_8[2]), .out_13(out_8[1]), .out_14(out_8[0]), .in_1(in_2), .in_2(in_3), .in_3(in_4),
    .in_4(in_5), .in_5(in_6), .in_6(in_7));
  LED led_5 (.in(out_8[1]));
  LED led_6 (.in(out_8[0]));
endmodule
